# Fritzing sketch GroupProjectPartsSchematic (saved by Fritzing 0.9.3b)
breadboards: 1

parts:
  Part1 = Adafruit VL530X Time of Flight Distance Sensor [part_number="Adafruit #3317"]
  Part2 = Arduino Uno (Rev3) - ICSP
  Grove_Analog_Microphone = IC, DIP package, 4 pins [chip_label=IC]
  Grove_Analog_Microphone_2 = IC, DIP package, 4 pins [chip_label=IC]
  TCS3200 = IC, DIP package, 8 pins [chip_label=IC]
  Grove_Analog_Microphone_3 = IC, DIP package, 4 pins [chip_label=IC]
  PCB = IC, DIP package, 8 pins [chip_label=PCB]

nets:
  GND: Part1.GND, Part2.GND, Grove_Analog_Microphone.pin2, Grove_Analog_Microphone_2.pin2, TCS3200.pin4, Grove_Analog_Microphone_3.pin2, PCB.pin5
  N1: Part1.SDA, Part2.A4/SDA
  N2: Part1.SCL, Part2.A5/SCL
  3.3V: Part1.VCC
  N3: Part2.A1, PCB.pin8
  N4: Part2.A2, PCB.pin7
  N5: Part2.A3, PCB.pin6
  N6: Part2.D8, TCS3200.pin6
  N7: Part2.D4, TCS3200.pin1
  N8: Part2.D5_PWM, TCS3200.pin2
  N9: Part2.D6_PWM, TCS3200.pin8
  N10: Part2.D7, TCS3200.pin7
  5V: Grove_Analog_Microphone.pin1, Grove_Analog_Microphone_2.pin1, TCS3200.pin5, Grove_Analog_Microphone_3.pin1, PCB.pin4
  N11: Grove_Analog_Microphone.pin4, PCB.pin2
  N12: Grove_Analog_Microphone_2.pin4, PCB.pin3
  N13: Grove_Analog_Microphone_3.pin4, PCB.pin1

custom parts:
  Adafruit VL530X Time of Flight Distance Sensor: The VL53L0X is a Time of Flight distance sensor like no other you've used! The sensor contains a very tiny invisible laser source, and a matching sensor. The VL53L0X can detect the "time of flight", or how long the light has taken to bounce back to the sensor. Since it uses a very narrow light source, it is good for determining distance of only the surface directly in front of it. Unlike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
